# Fritzing sketch Project_Veroboard_Sketch (saved by Fritzing 0.9.3b)
stripboards: 1

parts:
  IC1 = IC, DIP package, 28 pins [chip_label=IC]
  JP1 = Header 1 [package=1x01_offset]
  JP2 = Header 1 [package=1x01_offset]
  JP3 = Header 1 [package=1x01_offset]
  JP5 = Header 1 [package=1x01_offset]
  C1 = Tantalum Capacitor [capacitance=10µF package="D 7343 [SMD, tantalum]"]
  JP6 = Header 1 [package=1x01_offset]
  JP7 = Header 1 [package=1x01_offset]  # not connected
  JP8 = Header 1 [package=1x01_offset]
  JP9 = Header 1 [package=1x01_offset]
  JP10 = Header 1 [package=1x01_offset]  # not connected
  JP11 = Header 1 [package=1x01_offset]  # not connected
  JP12 = Header 1 [package=1x01_offset]
  JP13 = Header 1 [package=1x01_offset]
  IC2 = V_REG_LD1117VXX [package=78xxl]
  C2 = Tantalum Capacitor [capacitance=10µF package="D 7343 [SMD, tantalum]"]
  C3 = Tantalum Capacitor [capacitance=10µF package="D 7343 [SMD, tantalum]"]
  JP15 = Header 1 [package=1x01_offset]
  C4 = Tantalum Capacitor [capacitance=10µF package="D 7343 [SMD, tantalum]"]
  R2 = Temperature Sensor (Thermistor) [thermistor_type=NTC package=THT]
  R3 = Temperature Sensor (Thermistor) [thermistor_type=NTC package=THT]
  R4 = Resistor [tolerance=±5% resistance=1k package=THT]
  R5 = Resistor [tolerance=±5% resistance=1k package=THT]
  C5 = Tantalum Capacitor [capacitance=10µF package="D 7343 [SMD, tantalum]"]
  JP14 = Header 1 [package=1x01_offset]
  R6 = Resistor [tolerance=±5% resistance=220 package=THT]
  JP4 = Header 1 [package=1x01_offset]

nets:
  N1: IC1.pin1, IC1.pin2, IC1.pin3, IC1.pin5, IC1.pin6, IC1.pin7, IC1.pin8, IC1.pin9, IC1.pin10, IC1.pin11, IC1.pin12, IC1.pin13, IC1.pin14, IC1.pin19, IC1.pin23, IC1.pin27, IC1.pin28, JP1.1, JP2.1, JP3.1, JP5.1, C1.-, JP6.1, JP8.1, JP13.1, IC2.OUT, IC2.IN, C2.-, C3.-, C3.+, JP15.1, C4.-, C4.+, R2.pin_0, R2.pin_1, R3.pin_0, R3.pin_1, R4.Pin_0, R4.Pin_1, R5.Pin_0, R5.Pin_1, C5.-, C5.+, R6.Pin_0, R6.Pin_1, JP4.1
  N2: IC1.pin17, JP9.1
  N3: IC1.pin18, JP12.1
  N4: IC1.pin20, C1.+
  N5: IC2.GND, C2.+, JP14.1
